# Fritzing sketch Thermometar_sch (saved by Fritzing 0.9.3b)
breadboards: 1

parts:
  Q1 = NPN-Transistor [package="TO92 [THT]"]
  Q2 = NPN-Transistor [package="TO92 [THT]"]
  Q3 = NPN-Transistor [package="TO92 [THT]"]
  Q4 = NPN-Transistor [package="TO92 [THT]"]
  Part2 = Arduino Nano (Rev3.0) (ICSP)
  U3 = Voltage Regulator - 5V [package="DPak [SMD]"]
  C2 = Electrolytic Capacitor [capacitance=220µF voltage=50V package="100 mil [THT, electrolytic]"]
  C3 = Electrolytic Capacitor [capacitance=47µF voltage=50V package="100 mil [THT, electrolytic]"]
  LM335z = LM335 Temperature Sensor [package="TO92 [THT]"]
  R1 = Resistor [tolerance=±5% resistance=2k package="0402 [SMD]"]
  LED1 = 7-SEGMENT-4DIGIT-YOUNGSUN [package=7-segment-4digit-youngsun-longpads]

nets:
  GND: Q1.E, Q2.E, Q3.E, Q4.E, Part2.GND, U3.GND, C2.-, C3.-, LM335z.GND
  N1: Q1.B, Part2.D10
  N2: Q1.C, LED1.DIG1
  N3: Q2.B, Part2.D11/MOSI
  N4: Q2.C, LED1.DIG4
  N5: Q3.B, Part2.D12/MISO
  N6: Q3.C, LED1.DIG3
  N7: Q4.B, Part2.D13/SCK
  N8: Q4.C, LED1.DIG2
  N9: Part2.D2, LED1.G
  N10: Part2.D3, LED1.C
  N11: Part2.D4, LED1.DP
  N12: Part2.D5, LED1.D
  N13: Part2.D6, LED1.E
  N14: Part2.D7, LED1.A
  N15: Part2.D8, LED1.F
  N16: Part2.D9, LED1.B
  N17: Part2.VIN, U3.output_voltage, C3.+
  N18: Part2.A0, R1.Pin_1
  N19: U3.input_voltage, C2.+
  N20: LM335z.Output, R1.Pin_0

custom parts:
  LM335 Temperature Sensor: A LM335 temperature sensor with a temperature range from -55°C to 150°C.

// code stored in the sketch: thermometar2.ino
sdf
sdgf
sdf

asdf
