# Fritzing sketch LedStribBoard (saved by Fritzing 0.9.3b)
breadboards: 1

parts:
  Button_minus_(-) = Pushbutton [package="[THT]"]
  Button_plus_(+) = Pushbutton [package="[THT]"]
  Nano = Arduino Nano (Rev3.0)
  C1 = Electrolytic Capacitor [capacitance=220µF voltage=50V package="100 mil [THT, electrolytic]"]
  U1 = Voltage Regulator - 5V [package="DPak [SMD]"]
  C2 = Electrolytic Capacitor [capacitance=47µF voltage=50V package="100 mil [THT, electrolytic]"]
  Q1 = npn-Powertransistor [package="TO220 [THT]"]
  D1 = Rectifier Diode 10A [part_number=P1000K]
  TSOP1736 = TSOP312.., 314.. [package=THT]
  R1 = Resistor [tolerance=±5% resistance=100k package="2512 [SMD]"]
  R2 = Resistor [tolerance=±5% resistance=100k package="2512 [SMD]"]
  Input_voltage_12Vdc_2A = Power plug
  12V_Output_PWM = Power plug

nets:
  N1: Button_minus_(-).Pin_1, Button_minus_(-).Pin_2, Nano.D4, R1.Pin_0
  N2: Button_minus_(-).Pin_3, Button_minus_(-).Pin_4, Button_plus_(+).Pin_3, Button_plus_(+).Pin_4, Nano.5V, TSOP1736.Vs
  N3: Button_plus_(+).Pin_1, Button_plus_(+).Pin_2, Nano.D3, R2.Pin_0
  GND: Nano.GND, C1.-, U1.GND, C2.-, TSOP1736.GND, R1.Pin_1, R2.Pin_1, Input_voltage_12Vdc_2A.GND, 12V_Output_PWM.GND
  N4: Nano.D10, Q1.base
  N5: Nano.D11/MOSI, TSOP1736.Data
  N6: Nano.VIN, U1.output_voltage, C2.+
  N7: C1.+, U1.input_voltage, Q1.collector, D1.cathode
  N8: Q1.emitter, 12V_Output_PWM.VCC
  N9: D1.anode, Input_voltage_12Vdc_2A.VCC

notes:
  Output to Led Strip.
  PWM to dim the leds
