# Fritzing sketch SensorBoard (saved by Fritzing 0.9.2b)
circuit board: 10.4764cm x 5.55813cm

parts:
  Part1 = Triple Axis Magnetometer - HMC5883 Breakout
  Part2 = Arduino Nano (Rev3.0)
  Part3 = SRF05 Ultrasonic Rangefinder
  Part4 = SRF05 Ultrasonic Rangefinder

nets:
  GND: Part1.GND, Part2.GND, Part3.GND, Part4.GND
  VCC: Part1.VCC, Part2.5V, Part4.VCC
  N1: Part1.SDA, Part2.A4
  N2: Part1.SCL, Part2.A5
  N3: Part2.D7, Part3.Echo
  N4: Part2.D8, Part3.Trig
  N5: Part2.D11/MOSI, Part4.Echo
  N6: Part2.D12/MISO, Part4.Trig
